# Fritzing sketch stockpi_breadboard_diagram (saved by Fritzing 0.8.7b)
breadboards: 1

parts:
  Raspberry_Pi_B_rev1 = Raspberry Pi B rev2
  R1 = Resistor [tolerance=±5% resistance=220 package=THT]
  R2 = Resistor [tolerance=±5% resistance=220 package=THT]
  R3 = Resistor [tolerance=±5% resistance=220 package=THT]
  LED1 = LED - 5mm [color="Green (555nm)" package="5 mm [THT]"]
  LED2 = LED - 5mm [color="Red (633nm)" package="5 mm [THT]"]
  LED3 = LED - 5mm [color="Blue (470nm)" package="5 mm [THT]"]

nets:
  N1: Raspberry_Pi_B_rev1.GND, R2.Pin_1
  N2: Raspberry_Pi_B_rev1.GPIO_17, LED1.anode
  N3: Raspberry_Pi_B_rev1.GPIO_27, LED2.anode
  N4: Raspberry_Pi_B_rev1.GPIO_4, LED3.anode
  N5: R1.Pin_0, LED3.cathode
  N6: R2.Pin_0, LED1.cathode
  N7: R3.Pin_0, LED2.cathode
